# Fritzing sketch 01_SimpleSwitchAndLight (saved by Fritzing 0.9.10b)
breadboards: 1

parts:
  S1 = Taiway 100-SP-X-T1 SPDT Miniature Toggle Switch [part_number=100-SP-X-T1-0-0-B1-M1 package=THT]
  LED1 = LED - 5mm [color="Red (633nm)" current=0.030 package="5 mm [THT]"]
  R1 = Resistor [tolerance=±5% power=0.25 resistance=220 package=THT]
  VCC1 = Battery

nets:
  N1: S1.L1, VCC1.+
  N2: S1.L2, R1.Pin_0
  N3: LED1.cathode, VCC1.-
  N4: LED1.anode, R1.Pin_1
